# Fritzing sketch calc_fz (saved by Fritzing 0.7.12b)
breadboards: 1

parts:
  Arduino1 = Arduino
  LCD1 = LCD screen
  R1 = Resistor [tolerance=±5% resistance=220 package=THT]

nets:
  N1: Arduino1.D11, LCD1.RS
  N2: Arduino1.D10, LCD1.E
  N3: Arduino1.D5, LCD1.DB4
  N4: Arduino1.D4, LCD1.DB5
  N5: Arduino1.D3, LCD1.DB6
  N6: Arduino1.D2, LCD1.DB7
  +5V: Arduino1.+5V, LCD1.VDD
  GND: Arduino1.GND, LCD1.VSS, LCD1.R/W, R1.Pin_1
  N7: LCD1.V0, R1.Pin_0

notes:
  Keypad connector
